# Fritzing sketch Breadboard design (saved by Fritzing 0.9.3b)
breadboards: 1

parts:
  M2 = DC Motor
  M3 = DC Motor
  M4 = DC Motor
  A1 = HC-SR04 Ultrasonic Distance Sensor
  A2 = HC-SR04 Ultrasonic Distance Sensor
  A3 = HC-SR04 Ultrasonic Distance Sensor
  Part1 = Arduino Mega 2560 (Rev3)-TopMount
  L298N1 = L298N DC motor driver
  M5 = DC Motor
  S1 = Round Pushbutton
  VCC1 = Battery block 9V

nets:
  N1: M2.pin_1, M3.pin_1, L298N1.OUT1
  N2: M2.pin_2, M3.pin_2, L298N1.OUT2
  N3: M4.pin_1, L298N1.OUT3, M5.pin_1
  N4: M4.pin_2, L298N1.OUT4, M5.pin_2
  VCC: A1.VCC, A2.VCC, A3.VCC, Part1.5V
  N5: A1.TRIG, Part1.D13_PWM
  N6: A1.ECHO, Part1.D12_PWM
  GND: A1.GND, A2.GND, A3.GND, Part1.GND
  N7: A2.TRIG, Part1.D10_PWM
  N8: A2.ECHO, Part1.D9_PWM
  N9: A3.TRIG, Part1.D22
  N10: A3.ECHO, Part1.D24
  N11: Part1.D32, L298N1.ENA
  N12: Part1.D34, L298N1.IN1
  N13: Part1.D36, L298N1.IN2
  N14: Part1.D38, L298N1.IN3
  N15: Part1.D40, L298N1.IN4
  N16: Part1.D42, L298N1.ENB
  N17: L298N1.12V, VCC1.+
  N18: L298N1.GND, S1.leg0
  N19: S1.leg1, VCC1.-

custom parts:
  HC-SR04 Ultrasonic Distance Sensor: The HC-SR04 is an ultrasonic distance sensor. It is capable of providing measurement for ranges of 2cm to 400cm. The module operates at 5V.
  Arduino Mega 2560 (Rev3)-TopMount: Arduino Mega 2560 (Rev3) for Top PCB Mount. The PCB view of the Arduino Mega 2560 (Rev3) in Arduino Bin flipped upside down with the text flipped back so as to be readable. Other views haven't changed Protruding component position is outlined to provide indication of part contact. Number in component outline is mm of protrusion of the component from the Mega PCB. Subtract the number from the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
  L298N DC motor driver: 2x DC motor driver with 78M05 positive voltage regulator (7..35 V) L298N: max 46 V, 2 A Set 5 V Enable jumper to enable 5 V regultor (needed for the L298N) and +5 V output at screw terminal or supply external +5 V at screw terminal Set ENA and/or ENB to +5 V to enable motor permanently or supply ENA and/or ENB with PWM signal IN1 and IN2 set rotation directory for motor A (OUT1/OUT2) IN2 and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
