# Fritzing sketch Schematic (saved by Fritzing 0.9.10)

parts:
  Power_Distribution_/_5V_Regulator = Power Distribution / 5V Regulator
  9V_Battery = 9V Battery
  SPST_Power_Switch = SPST Power Switch
  Arduino_Mega_2560 = Arduino Mega 2560
  L298N_Dual_H-Bridge = L298N Dual H-Bridge
  HC-SR04_FRONT = HC-SR04 (FRONT)
  HC-SR04_LEFT = HC-SR04 (LEFT)
  HC-SR04_RIGHT = HC-SR04 (RIGHT)
  Motor_FRONT-LEFT = DC Motor FRONT LEFT
  Motor_REAR-LEFT = DC Motor REAR LEFT
  Motor_FRONT-RIGHT = DC Motor FRONT RIGHT
  Motor_REAR-RIGHT = DC Motor REAR RIGHT

nets:
  N1: Power_Distribution_/_5V_Regulator.BAT+, SPST_Power_Switch.OUT
  N2: Power_Distribution_/_5V_Regulator.BAT-, 9V_Battery.B-
  VCC: Power_Distribution_/_5V_Regulator.+5V, Arduino_Mega_2560.+5V, HC-SR04_FRONT.VCC, HC-SR04_LEFT.VCC, HC-SR04_RIGHT.VCC
  GND: Power_Distribution_/_5V_Regulator.GND, HC-SR04_FRONT.GND, HC-SR04_LEFT.GND, HC-SR04_RIGHT.GND
  N3: Power_Distribution_/_5V_Regulator.MOTOR+, L298N_Dual_H-Bridge.+MOTOR
  GND_2: Power_Distribution_/_5V_Regulator.GND-, Arduino_Mega_2560.GND, L298N_Dual_H-Bridge.GND
  N4: 9V_Battery.B+, SPST_Power_Switch.IN
  N5: Arduino_Mega_2560.D30_FRONT_TRIG, HC-SR04_FRONT.TRIG
  N6: Arduino_Mega_2560.D31_FRONT_ECHO, HC-SR04_FRONT.ECHO
  N7: Arduino_Mega_2560.D32_LEFT_TRIG, HC-SR04_LEFT.TRIG
  N8: Arduino_Mega_2560.D33_LEFT_ECHO, HC-SR04_LEFT.ECHO
  N9: Arduino_Mega_2560.D34_RIGHT_TRIG, HC-SR04_RIGHT.TRIG
  N10: Arduino_Mega_2560.D35_RIGHT_ECHO, HC-SR04_RIGHT.ECHO
  N11: Arduino_Mega_2560.D24_IN1, L298N_Dual_H-Bridge.IN1
  N12: Arduino_Mega_2560.D25_IN2, L298N_Dual_H-Bridge.IN2
  N13: Arduino_Mega_2560.D26_IN3, L298N_Dual_H-Bridge.IN3
  N14: Arduino_Mega_2560.D27_IN4, L298N_Dual_H-Bridge.IN4
  N15: Arduino_Mega_2560.D5_ENA, L298N_Dual_H-Bridge.ENA
  N16: Arduino_Mega_2560.D6_ENB, L298N_Dual_H-Bridge.ENB
  N17: L298N_Dual_H-Bridge.OUT1, Motor_FRONT-LEFT.M+, Motor_REAR-LEFT.M+
  N18: L298N_Dual_H-Bridge.OUT2, Motor_FRONT-LEFT.M-, Motor_REAR-LEFT.M-
  N19: L298N_Dual_H-Bridge.OUT3, Motor_FRONT-RIGHT.M+, Motor_REAR-RIGHT.M+
  N20: L298N_Dual_H-Bridge.OUT4, Motor_FRONT-RIGHT.M-, Motor_REAR-RIGHT.M-
